// Logisim project ALU_4bit.circ as structural Verilog: 1 circuit, main circuit alu
module alu (
  input  [3:0] in_1,
  input  [3:0] in_2,
  input  [1:0] in_3,
  output [3:0] out_4
);

  wire [3:0] add, \and , \or , sub;

  Adder #(.width(4)) adder_1 (.a(in_1), .b(in_2), .out(add));  // open: cin, cout
  Subtractor #(.width(4)) subtractor_1 (.a(in_1), .b(in_2), .out(sub));  // open: bin, bout
  assign \and  = in_1 & in_2;  // AND_Gate and_1, 4 bits wide
  assign \or  = in_1 | in_2;  // OR_Gate or_1, 4 bits wide
  Multiplexer #(.select(2), .width(4), .enable("false")) multiplexer_1 (
    .in0(add), .in1(sub), .in2(\and ), .in3(\or ), .out(out_4), .sel(in_3));

  // Other names for the same wires on the sheet: a[3:0] = in_1; b[3:0] = in_2; sel[1:0] = in_3
endmodule
