// Logisim project CPU.circ as structural Verilog: 10 circuits, main circuit main
module main (
  input  in_1,
  output [31:0] out_2,
  output out_3,
  output [4:0] out_4,
  output [31:0] out_5,
  output out_6,
  output [4:0] out_7,
  output [31:0] out_8
);

  wire ALUsrc, DMtoReg, ExtOp, NPC_SL, RegDst, ZERO;
  wire [1:0] ALUctr;
  wire [4:0] rd, rs, rt;
  wire [5:0] FUNC, OPCODE;
  wire [15:0] IMM16;
  wire [31:0] alu_1_alu_result, dm_1_dout, ext_1_ext_out, grf_1_rs_out, multiplexer_2_out;

  Controller controller_1 (
    .opcode(OPCODE), .func(FUNC), .RegDst(RegDst), .NPC_SL(NPC_SL), .DMtoReg(DMtoReg), .RegWr(out_3),
    .ExtOp(ExtOp), .ALUsrc(ALUsrc), .DMWr(out_6), .ALUOp(ALUctr));
  IFU ifu_1 (.Reset(in_1), .ZERO(ZERO), .NPC_SL(NPC_SL), .IMM16(IMM16), .INS(out_2));
  DECODE decode_1 (.in_1(out_2), .func(FUNC), .rd(rd), .rt(rt), .rs(rs), .opcode(OPCODE), .imm(IMM16));
  Multiplexer #(.width(5), .disabled(0), .enable("false")) multiplexer_1 (
    .in0(rt), .in1(rd), .out(out_4), .sel(RegDst));
  GRF grf_1 (
    .WD(out_5), .RW(out_4), .rs(rs), .rt(rt), .RegWr(out_3), .Reset(in_1), .RS_OUT(grf_1_rs_out),
    .RT_OUT(out_8));
  EXT ext_1 (.Ext_Op(ExtOp), .IMM16(IMM16), .EXT_OUT(ext_1_ext_out));
  ALU alu_1 (
    .in_1(ALUctr), .IUPUT_A(grf_1_rs_out), .IUPUT_B(multiplexer_2_out), .ZERO(ZERO),
    .ALU_result(alu_1_alu_result));
  Multiplexer #(.width(32), .enable("false")) multiplexer_2 (
    .in0(out_8), .in1(ext_1_ext_out), .out(multiplexer_2_out), .sel(ALUsrc));
  Multiplexer #(.width(32), .disabled(0), .enable("false")) multiplexer_3 (
    .in0(alu_1_alu_result), .in1(dm_1_dout), .out(out_5), .sel(DMtoReg));
  DM dm_1 (.DIN(out_8), .AD(alu_1_alu_result), .DMWr(out_6), .Reset(in_1), .out_6(out_7), .DOUT(dm_1_dout));

  // Other names for the same wires on the sheet: DIN[31:0] = out_8; DMWr = out_6; Instr[31:0] = out_2;
  //   MemAddr[4:0] = out_7; RegAddr[4:0] = out_4; RegData[31:0] = out_5; RegWr = out_3; Reset = in_1
endmodule

module ALU (
  input  [1:0] in_1,
  input  [31:0] IUPUT_A,
  input  [31:0] IUPUT_B,
  output ZERO,
  output [31:0] ALU_result
);

  wire [31:0] add, lui, \or , sub;

  Comparator #(.width(32)) comparator_1 (.a(IUPUT_A), .b(IUPUT_B), .eq(ZERO));  // open: gt, lt
  Adder #(.width(32)) adder_1 (.a(IUPUT_A), .b(IUPUT_B), .out(add));  // open: cin, cout
  Subtractor #(.width(32)) subtractor_1 (.a(IUPUT_A), .b(IUPUT_B), .out(sub));  // open: bin, bout
  assign \or  = IUPUT_A | IUPUT_B;  // OR_Gate or_1, 32 bits wide
  Shifter #(.width(32)) shifter_1 (.in(IUPUT_B), .\dist (5'b10000), .out(lui));
  Multiplexer #(.select(2), .width(32), .disabled(0)) multiplexer_1 (
    .in0(add), .in1(sub), .in2(\or ), .in3(lui), .out(ALU_result), .sel(in_1));  // open: en

  // Other names for the same wires on the sheet: ALUOp[1:0] = in_1; input1[31:0] = IUPUT_A; input2[31:0] = IUPUT_B
endmodule

module EXT (
  input  Ext_Op,
  input  [15:0] IMM16,
  output [31:0] EXT_OUT
);

  wire [31:0] bit_extender_1_out, bit_extender_2_out;

  assign bit_extender_1_out = {{16{1'b0}}, IMM16};  // Bit_Extender bit_extender_1
  assign bit_extender_2_out = {{16{IMM16[15]}}, IMM16};  // Bit_Extender bit_extender_2
  Multiplexer #(.width(32), .disabled(0), .enable("false")) multiplexer_1 (
    .in0(bit_extender_1_out), .in1(bit_extender_2_out), .out(EXT_OUT), .sel(Ext_Op));

  // Other names for the same wires on the sheet: control = Ext_Op
endmodule

module DM (
  input  [31:0] DIN,
  input  [31:0] AD,
  input  DMWr,
  input  Reset,
  output [31:0] DOUT,
  output [4:0] out_6
);

  wire CHIP_0, CLK;
  wire [4:0] CHIP, WORD;
  wire [31:0] subtractor_1_out;

  Clock clock_1 (.out(CLK));
  Subtractor #(.width(32)) subtractor_1 (
    .a(AD), .b(32'h2000), .out({subtractor_1_out[31:12], CHIP, WORD, subtractor_1_out[1:0]}));  // open: bin, bout
  RAM #(.addrWidth(5), .dataWidth(32), .bus("separate")) ram_1 (
    .addr(AD[6:2]), .din(DIN), .data(DOUT), .str(DMWr), .clk(CLK), .clr(Reset));  // open: sel, ld
  Decoder #(.select(5)) decoder_1 (
    .out0(CHIP_0), .sel(CHIP));  // open: out1, out2, out3, out4, out5, out6, out7, out8, out9, out10, out11, out12, out13, out14, out15, out16, out17, out18, out19, out20, out21, out22, out23, out24, out25, out26, out27, out28, out29, out30, out31, en

  assign out_6 = AD[6:2];

  // Other names for the same wires on the sheet: DATA_IN[31:0] = DIN
endmodule

module IFU (
  input  Reset,
  input  ZERO,
  input  NPC_SL,
  input  [15:0] IMM16,
  output [31:0] INS
);

  wire and_1_out, CLK;
  wire [31:0] adder_2_out, bit_extender_1_out, multiplexer_1_out, PC, PC_4, shifter_1_out;

  Clock clock_1 (.out(CLK));
  assign bit_extender_1_out = {{16{IMM16[15]}}, IMM16};  // Bit_Extender bit_extender_1
  Shifter #(.width(32)) shifter_1 (.in(bit_extender_1_out), .\dist (5'b00010), .out(shifter_1_out));
  Adder #(.width(32)) adder_1 (.a(PC), .b(32'h4), .out(PC_4));  // open: cin, cout
  and and_1 (and_1_out, ZERO, NPC_SL);
  Adder #(.width(32)) adder_2 (.a(PC_4), .b(shifter_1_out), .out(adder_2_out));  // open: cin, cout
  // Probe on multiplexer_1_out
  Register #(.width(32)) u_PC (.D(multiplexer_1_out), .Q(PC), .clk(CLK), .clr(Reset));  // open: en
  Multiplexer #(.width(32), .disabled(0), .enable("false")) multiplexer_1 (
    .in0(PC_4), .in1(adder_2_out), .out(multiplexer_1_out), .sel(and_1_out));
  ROM #(.addrWidth(5), .dataWidth(32)) rom_1 (.addr(PC[6:2]), .data(INS));  // open: sel

  // Other names for the same wires on the sheet: imm[15:0] = IMM16

  // Notes on the sheet:
  //   IM
  //   contents of rom_1 (hex, n*v repeats v):
  //   3c080004 3c090008 340b2004 ad680004 1495021 8d6c0004 3c0d0004 1cd7823 10d4021 1c87021 1109fff9
  //   10d4021 3c020001 3c030002 431021 431821 3444ffff 623023 c52821 10a3fffd
endmodule

module GRF (
  input  [31:0] WD,
  input  [4:0] RW,
  input  [4:0] rs,
  input  [4:0] rt,
  input  RegWr,
  input  Reset,
  output [31:0] RS_OUT,
  output [31:0] RT_OUT
);

  wire CLK, WE0, WE1, WE2, WE3, WE4, WE5, WE6, WE7, WE8, WE9, WE10, WE11, WE12, WE13, WE14, WE15, WE16, WE17,
       WE18, WE19, WE20, WE21, WE22, WE23, WE24, WE25, WE26, WE27, WE28, WE29, WE30, WE31;
  wire [31:0] out0, out1, out2, out3, out4, out5, out6, out7, out8, out9, out10, out11, out12, out13, out14,
       out15, out16, out17, out18, out19, out20, out21, out22, out23, out24, out25, out26, out27, out28,
       out29, out30, out31;

  Clock clock_1 (.out(CLK));
  Decoder #(.select(5), .disabled(0)) decoder_1 (
    .out0(WE0), .out1(WE1), .out2(WE2), .out3(WE3), .out4(WE4), .out5(WE5), .out6(WE6), .out7(WE7),
    .out8(WE8), .out9(WE9), .out10(WE10), .out11(WE11), .out12(WE12), .out13(WE13), .out14(WE14),
    .out15(WE15), .out16(WE16), .out17(WE17), .out18(WE18), .out19(WE19), .out20(WE20), .out21(WE21),
    .out22(WE22), .out23(WE23), .out24(WE24), .out25(WE25), .out26(WE26), .out27(WE27), .out28(WE28),
    .out29(WE29), .out30(WE30), .out31(WE31), .sel(RW), .en(RegWr));
  Register #(.width(32)) register_1 (.D({32{1'b0}}), .en(WE0), .Q(out0), .clk(CLK));  // open: clr
  Register #(.width(32)) register_2 (.D(WD), .en(WE1), .Q(out1), .clk(CLK), .clr(Reset));
  Register #(.width(32)) register_3 (.D(WD), .en(WE3), .Q(out3), .clk(CLK), .clr(Reset));
  Register #(.width(32)) register_4 (.D(WD), .en(WE5), .Q(out5), .clk(CLK), .clr(Reset));
  Register #(.width(32)) register_5 (.D(WD), .en(WE7), .Q(out7), .clk(CLK), .clr(Reset));
  Register #(.width(32)) register_6 (.D(WD), .en(WE9), .Q(out9), .clk(CLK), .clr(Reset));
  Register #(.width(32)) register_7 (.D(WD), .en(WE11), .Q(out11), .clk(CLK), .clr(Reset));
  Register #(.width(32)) register_8 (.D(WD), .en(WE13), .Q(out13), .clk(CLK), .clr(Reset));
  Register #(.width(32)) register_9 (.D(WD), .en(WE15), .Q(out15), .clk(CLK), .clr(Reset));
  Register #(.width(32)) register_10 (.D(WD), .en(WE17), .Q(out17), .clk(CLK), .clr(Reset));
  Register #(.width(32)) register_11 (.D(WD), .en(WE19), .Q(out19), .clk(CLK), .clr(Reset));
  Register #(.width(32)) register_12 (.D(WD), .en(WE21), .Q(out21), .clk(CLK), .clr(Reset));
  Register #(.width(32)) register_13 (.D(WD), .en(WE23), .Q(out23), .clk(CLK), .clr(Reset));
  Register #(.width(32)) register_14 (.D(WD), .en(WE25), .Q(out25), .clk(CLK), .clr(Reset));
  Register #(.width(32)) register_15 (.D(WD), .en(WE27), .Q(out27), .clk(CLK), .clr(Reset));
  Register #(.width(32)) register_16 (.D(WD), .en(WE29), .Q(out29), .clk(CLK), .clr(Reset));
  Register #(.width(32)) register_17 (.D(WD), .en(WE31), .Q(out31), .clk(CLK), .clr(Reset));
  Register #(.width(32)) register_18 (.D(WD), .en(WE2), .Q(out2), .clk(CLK), .clr(Reset));
  Register #(.width(32)) register_19 (.D(WD), .en(WE4), .Q(out4), .clk(CLK), .clr(Reset));
  Register #(.width(32)) register_20 (.D(WD), .en(WE6), .Q(out6), .clk(CLK), .clr(Reset));
  Register #(.width(32)) register_21 (.D(WD), .en(WE8), .Q(out8), .clk(CLK), .clr(Reset));
  Register #(.width(32)) register_22 (.D(WD), .en(WE10), .Q(out10), .clk(CLK), .clr(Reset));
  Register #(.width(32)) register_23 (.D(WD), .en(WE12), .Q(out12), .clk(CLK), .clr(Reset));
  Register #(.width(32)) register_24 (.D(WD), .en(WE14), .Q(out14), .clk(CLK), .clr(Reset));
  Register #(.width(32)) register_25 (.D(WD), .en(WE16), .Q(out16), .clk(CLK), .clr(Reset));
  Register #(.width(32)) register_26 (.D(WD), .en(WE18), .Q(out18), .clk(CLK), .clr(Reset));
  Register #(.width(32)) register_27 (.D(WD), .en(WE20), .Q(out20), .clk(CLK), .clr(Reset));
  Register #(.width(32)) register_28 (.D(WD), .en(WE22), .Q(out22), .clk(CLK), .clr(Reset));
  Register #(.width(32)) register_29 (.D(WD), .en(WE24), .Q(out24), .clk(CLK), .clr(Reset));
  Register #(.width(32)) register_30 (.D(WD), .en(WE26), .Q(out26), .clk(CLK), .clr(Reset));
  Register #(.width(32)) register_31 (.D(WD), .en(WE28), .Q(out28), .clk(CLK), .clr(Reset));
  Register #(.width(32)) register_32 (.D(WD), .en(WE30), .Q(out30), .clk(CLK), .clr(Reset));
  Multiplexer #(.select(5), .width(32), .disabled(0)) multiplexer_1 (
    .in0(out0), .in1(out1), .in2(out2), .in3(out3), .in4(out4), .in5(out5), .in6(out6), .in7(out7),
    .in8(out8), .in9(out9), .in10(out10), .in11(out11), .in12(out12), .in13(out13), .in14(out14),
    .in15(out15), .in16(out16), .in17(out17), .in18(out18), .in19(out19), .in20(out20), .in21(out21),
    .in22(out22), .in23(out23), .in24(out24), .in25(out25), .in26(out26), .in27(out27), .in28(out28),
    .in29(out29), .in30(out30), .in31(out31), .out(RS_OUT), .sel(rs));  // open: en
  Multiplexer #(.select(5), .width(32), .disabled(0)) multiplexer_2 (
    .in0(out0), .in1(out1), .in2(out2), .in3(out3), .in4(out4), .in5(out5), .in6(out6), .in7(out7),
    .in8(out8), .in9(out9), .in10(out10), .in11(out11), .in12(out12), .in13(out13), .in14(out14),
    .in15(out15), .in16(out16), .in17(out17), .in18(out18), .in19(out19), .in20(out20), .in21(out21),
    .in22(out22), .in23(out23), .in24(out24), .in25(out25), .in26(out26), .in27(out27), .in28(out28),
    .in29(out29), .in30(out30), .in31(out31), .out(RT_OUT), .sel(rt));  // open: en

  // Other names for the same wires on the sheet: RD[4:0] = RW; WB[31:0] = WD
endmodule

module PC (
  input  Reset,
  input  ZERO,
  input  NPC_SL,
  input  [15:0] IMM16,
  output [31:0] PC
);

  wire and_1_out, CLK;
  wire [31:0] adder_2_out, bit_extender_1_out, multiplexer_1_out, PC_4, shifter_1_out;

  Clock clock_1 (.out(CLK));
  assign bit_extender_1_out = {{16{IMM16[15]}}, IMM16};  // Bit_Extender bit_extender_1
  Shifter #(.width(32)) shifter_1 (.in(bit_extender_1_out), .\dist (5'b00010), .out(shifter_1_out));
  Adder #(.width(32)) adder_1 (.a(PC), .b(32'h4), .out(PC_4));  // open: cin, cout
  Adder #(.width(32)) adder_2 (.a(PC_4), .b(shifter_1_out), .out(adder_2_out));  // open: cin, cout
  Multiplexer #(.width(32), .disabled(0), .enable("false")) multiplexer_1 (
    .in0(PC_4), .in1(adder_2_out), .out(multiplexer_1_out), .sel(and_1_out));
  and and_1 (and_1_out, Reset, NPC_SL);
  Register #(.width(32)) u_PC (.D(multiplexer_1_out), .Q(PC), .clk(CLK), .clr(Reset));  // open: en

  // Other names for the same wires on the sheet: imm[15:0] = IMM16
endmodule

// decode
module DECODE (
  input  [31:0] in_1,
  output [5:0] func,
  output [4:0] rd,
  output [4:0] rt,
  output [4:0] rs,
  output [5:0] opcode,
  output [15:0] imm
);


  assign func = in_1[5:0];
  assign imm = in_1[15:0];
  assign opcode = in_1[31:26];
  assign rd = in_1[15:11];
  assign rs = in_1[25:21];
  assign rt = in_1[20:16];
endmodule

module Controller (
  input  [5:0] opcode,
  input  [5:0] func,
  output RegDst,
  output NPC_SL,
  output DMtoReg,
  output RegWr,
  output ExtOp,
  output ALUsrc,
  output DMWr,
  output [1:0] ALUOp
);

  wire decode_and_1_addu, decode_and_1_beq, decode_and_1_lui, decode_and_1_lw, decode_and_1_ori,
       decode_and_1_subu, decode_and_1_sw;

  decode_and decode_and_1 (
    .op5(opcode[5]), .op4(opcode[4]), .op3(opcode[3]), .op2(opcode[2]), .op1(opcode[1]), .op0(opcode[0]),
    .f5(func[5]), .f4(func[4]), .f3(func[3]), .f2(func[2]), .f1(func[1]), .f0(func[0]),
    .addu(decode_and_1_addu), .subu(decode_and_1_subu), .beq(decode_and_1_beq), .ori(decode_and_1_ori),
    .sw(decode_and_1_sw), .lw(decode_and_1_lw), .lui(decode_and_1_lui));
  or u_RegDst (RegDst, decode_and_1_addu, decode_and_1_subu);
  buf u_NPC_SL (NPC_SL, decode_and_1_beq);  // OR_Gate
  buf u_DMtoReg (DMtoReg, decode_and_1_lw);  // OR_Gate
  or u_RegWr (RegWr, decode_and_1_addu, decode_and_1_subu, decode_and_1_lui, decode_and_1_ori, decode_and_1_lw);
  or u_ExtOp (ExtOp, decode_and_1_lw, decode_and_1_sw);
  or u_ALUsrc (ALUsrc, decode_and_1_ori, decode_and_1_sw, decode_and_1_lui, decode_and_1_lw);
  buf u_DMWr (DMWr, decode_and_1_sw);  // OR_Gate
  or ALUOp1 (ALUOp[1], decode_and_1_ori, decode_and_1_lui);
  or ALUOp0 (ALUOp[0], decode_and_1_subu, decode_and_1_beq, decode_and_1_lui);

  // Notes on the sheet:
  //   ADD:00,SUB:01,ORI:10,LUI:11
endmodule

// AND
module decode_and (
  input  op5,
  input  op4,
  input  op3,
  input  op2,
  input  op1,
  input  op0,
  input  f5,
  input  f4,
  input  f3,
  input  f2,
  input  f1,
  input  f0,
  output addu,
  output subu,
  output beq,
  output ori,
  output sw,
  output lw,
  output lui
);

  wire not_1_out, not_2_out, not_3_out, not_4_out, not_5_out, not_6_out, not_7_out, not_8_out, not_9_out,
       not_10_out, not_11_out, not_12_out, Rtype_out;

  not not_1 (not_1_out, op5);
  not not_2 (not_2_out, op4);
  not not_3 (not_3_out, op3);
  not not_4 (not_4_out, op2);
  not not_5 (not_5_out, op1);
  not not_6 (not_6_out, op0);
  and Rtype (Rtype_out, not_1_out, not_2_out, not_3_out, not_4_out, not_5_out, not_5_out);
  not not_7 (not_7_out, f5);
  not not_8 (not_8_out, f4);
  not not_9 (not_9_out, f3);
  not not_10 (not_10_out, f2);
  not not_11 (not_11_out, f1);
  not not_12 (not_12_out, f0);
  and u_addu (addu, f5, not_8_out, not_9_out, not_10_out, not_11_out, f0, Rtype_out);
  and u_subu (subu, Rtype_out, f5, not_8_out, not_9_out, not_10_out, f1, f0);
  and u_beq (beq, not_1_out, not_2_out, not_3_out, op2, not_5_out, not_6_out);
  and u_ori (ori, not_1_out, not_2_out, op3, op2, not_5_out, op0);
  and u_sw (sw, op5, not_2_out, op3, not_4_out, op1, op0);
  and u_lw (lw, op5, not_2_out, not_3_out, not_4_out, op1, op0);
  and u_lui (lui, not_1_out, not_2_out, op3, op2, op1, op0);
endmodule
