// Logisim project CRC_code.circ as structural Verilog: 2 circuits, main circuit mod2_div
module mod2_div (
  input  [3:0] dividend,
  input  [3:0] divider,
  output [2:0] out_3,
  output out_4
);

  wire judge;
  wire [3:0] xor_1_out;

  and and_1 (judge, 1'b1, dividend[3]);
  assign xor_1_out = dividend ^ divider;  // XOR_Gate xor_1, 4 bits wide
  and and_2 (out_4, 1'b1, judge);
  Multiplexer #(.width(3), .enable("false")) multiplexer_1 (
    .in0(dividend[2:0]), .in1(xor_1_out[2:0]), .out(out_3), .sel(judge));

  // Other names for the same wires on the sheet: in1[3:0] = dividend; in2[3:0] = divider
endmodule

module CRC (
  input  [7:0] dividend,
  input  [3:0] divider,
  output [10:0] out_3
);

  wire [2:0] mod2_div_1_out_3, mod2_div_2_out_3, mod2_div_3_out_3, mod2_div_4_out_3;

  mod2_div mod2_div_1 (.dividend(dividend[7:4]), .divider(divider), .out_3(mod2_div_1_out_3));  // open: out_4
  mod2_div mod2_div_2 (
    .dividend({mod2_div_1_out_3, dividend[3]}), .divider(divider), .out_3(mod2_div_2_out_3));  // open: out_4
  mod2_div mod2_div_3 (
    .dividend({mod2_div_2_out_3, dividend[2]}), .divider(divider), .out_3(mod2_div_3_out_3));  // open: out_4
  mod2_div mod2_div_4 (
    .dividend({mod2_div_3_out_3, dividend[1]}), .divider(divider), .out_3(mod2_div_4_out_3));  // open: out_4
  mod2_div mod2_div_5 (
    .dividend({mod2_div_4_out_3, dividend[0]}), .divider(divider), .out_3(out_3[2:0]));  // open: out_4

  assign out_3[10:3] = dividend;

  // Other names for the same wires on the sheet: b[3:0] = divider; a[7:0] = dividend; a0 = dividend[0];
  //   a1 = dividend[1]; a2 = dividend[2]; a3 = dividend[3]; a4[3:0] = dividend[7:4]
endmodule
