// Logisim project FIBONA.circ as structural Verilog: 2 circuits, main circuit ADD
module ADD (
  input  in_1,
  input  in_2,
  output [4:0] out_3,
  output [4:0] out_4
);

  wire bit_extender_2_out, not_1_out;
  wire [4:0] adder_1_out, nor_1_out, OUT, Q;

  Adder #(.width(5)) adder_1 (.a(out_3), .b(Q), .out(adder_1_out));  // open: cin, cout
  Adder #(.width(5)) adder_2 (.a(adder_1_out), .b(out_4), .out(OUT));  // open: cin, cout
  Register #(.width(5)) register_1 (.D(OUT), .en(in_2), .Q(out_3), .clk(in_1));  // open: clr
  Register #(.width(5)) register_2 (.D(OUT), .en(in_2), .Q(out_4), .clk(not_1_out));  // open: clr
  not not_1 (not_1_out, in_1);
  assign nor_1_out = ~(out_3 | out_4);  // NOR_Gate nor_1, 5 bits wide
  assign Q = {{4{1'b0}}, bit_extender_2_out};  // Bit_Extender bit_extender_1
  Bit_Extender #(.in_width(5), .out_width(1)) bit_extender_2 (.in(nor_1_out), .out(bit_extender_2_out));

  // Other names for the same wires on the sheet: CLK = in_1; E = in_2
endmodule

module main (
  output [3:0] out_1
);

  wire bit_extender_1_out, CLK, clock_1_out, comparator_1_eq, not_1_out, not_2_out, not_3_out;
  wire [2:0] counter_1_q;
  wire [4:0] adder_1_out, D, nor_1_out, OUT, Q, register_1_q;
  wire [4:4] P;

  Clock clock_1 (.out(clock_1_out));
  assign CLK = not_1_out ? clock_1_out : 1'bz;  // Controlled_Buffer controlled_buffer_1
  Adder #(.width(5)) adder_1 (.a(D), .b(Q), .out(adder_1_out));  // open: cin, cout
  Counter #(.width(3), .max('h7)) counter_1 (
    .load(1'b0), .D(3'b110), .Q(counter_1_q), .clk(CLK));  // open: count, carry, clr
  Adder #(.width(5)) adder_2 (.a(adder_1_out), .b(register_1_q), .out(OUT));  // open: cin, cout
  not not_1 (not_1_out, comparator_1_eq);
  Comparator #(.width(3), .mode("unsigned")) comparator_1 (
    .a(3'b110), .b(counter_1_q), .eq(comparator_1_eq));  // open: gt, lt
  Register #(.width(5)) _1 (.D(OUT), .Q({P[4], out_1}), .clk(CLK));  // open: en, clr
  Register #(.width(5)) _2 (.D({P[4], out_1}), .Q(D), .clk(not_2_out));  // open: en, clr
  not not_2 (not_2_out, CLK);
  Register #(.width(5)) register_1 (.D(D), .Q(register_1_q), .clk(not_3_out));  // open: en, clr
  not not_3 (not_3_out, CLK);
  Bit_Extender #(.in_width(5), .out_width(1)) bit_extender_1 (.in(nor_1_out), .out(bit_extender_1_out));
  assign nor_1_out = ~(D | register_1_q);  // NOR_Gate nor_1, 5 bits wide
  assign Q = {{4{1'b0}}, bit_extender_1_out};  // Bit_Extender bit_extender_2

  // Other names for the same wires on the sheet: P[3:0] = out_1
endmodule
