// Logisim project RS_suocunqi.circ as structural Verilog: 1 circuit, main circuit main
module main (
  input  R,
  input  S,
  output Q,
  output Q1
);

  wire or_1_out, or_2_out;

  not not_1 (Q, or_1_out);
  or or_1 (or_1_out, R, Q1);
  or or_2 (or_2_out, Q, S);
  not not_2 (Q1, or_2_out);
endmodule
