// Logisim project enable.circ as structural Verilog: 1 circuit, main circuit main
module main (
  input  \input ,
  input  enable,
  input  input_2,
  input  enable_2,
  output \output ,
  output output_2
);

  assign \output  = enable ? ~\input  : 1'bz;  // Controlled_Inverter controlled_inverter_1
  and and_1 (output_2, input_2, input_2, enable_2);

  // Notes on the sheet:
  //   floating
  //   zero
endmodule
