// Logisim project fsm_p0.circ as structural Verilog: 4 circuits, main circuit fsm
module fsm (
  input  in_1,
  input  [1:0] in_2,
  output out_3
);

  wire buffer_1_out, buffer_2_out, clk, clr_t, register_2_q;
  wire [1:0] register_1_q, sec_state_1_f;

  Clock clock_1 (.out(clk));
  sec_state sec_state_1 (
    .a(register_1_q[1]), .b(register_1_q[0]), .c(in_2[1]), .d(in_2[0]), .e(sec_state_1_f[1]),
    .f(sec_state_1_f[0]));
  Register #(.width(2)) register_1 (.D(sec_state_1_f), .Q(register_1_q), .clk(clk), .clr(clr_t));  // open: en
  \output  output_1 (.a(register_1_q[1]), .b(register_1_q[0]), .c(in_2[1]), .d(in_2[0]), .e(out_3));
  Register #(.width(1)) register_2 (.D(1'b1), .Q(register_2_q), .clk(clk), .clr(buffer_1_out));  // open: en
  buf buffer_1 (buffer_1_out, buffer_2_out);
  buf buffer_2 (buffer_2_out, clk);
  and and_1 (clr_t, register_2_q, in_1);

  // Other names for the same wires on the sheet: CLR = in_1; input[1:0] = in_2
endmodule

module sec_state (
  input  a,
  input  b,
  input  c,
  input  d,
  output e,
  output f
);

  wire and_1_out, and_2_out, and_3_out, and_4_out, not_1_out, not_2_out, not_3_out, not_4_out, not_5_out,
       not_6_out, not_7_out;

  not not_1 (not_1_out, a);
  and and_1 (and_1_out, not_1_out, b, not_2_out);
  not not_2 (not_2_out, d);
  not not_3 (not_3_out, b);
  and and_2 (and_2_out, a, not_3_out, not_4_out);
  not not_4 (not_4_out, d);
  not not_5 (not_5_out, c);
  and and_3 (and_3_out, not_5_out, d);
  not not_6 (not_6_out, b);
  and and_4 (and_4_out, a, not_6_out, not_7_out);
  not not_7 (not_7_out, d);
  or or_1 (e, and_1_out, and_2_out);
  or or_2 (f, and_3_out, and_4_out);

  // Notes on the sheet:
  //   a,b as state,  c,d as input,  e,f as output
endmodule

module \output  (
  input  a,
  input  b,
  input  c,
  input  d,
  output e
);

  wire not_1_out, not_2_out;

  not not_1 (not_1_out, b);
  and and_1 (e, a, not_1_out, not_2_out);
  not not_2 (not_2_out, d);
endmodule

module fsm1 (
  input  in_1,
  input  [1:0] in_2,
  output out_3
);

  wire clk, clr1, clr2, comparator_1_gt, comparator_1_lt, comparator_2_gt, comparator_2_lt, counter_1_q,
       counter_2_q, not_1_out, not_2_out, or_1_out, Q, re, register_1_q;
  wire [1:0] register_3_q, sec_state_1_f;

  Clock clock_1 (.out(clk));
  Counter #(.width(1), .max('h1)) counter_1 (.Q(counter_1_q), .clk(clk));  // open: load, D, count, carry, clr
  Counter #(.width(1), .max('h1)) counter_2 (.Q(counter_2_q), .clk(in_1), .clr(Q));  // open: load, D, count, carry
  Register #(.width(1)) register_1 (.D(counter_1_q), .Q(register_1_q), .clk(not_1_out));  // open: en, clr
  not not_1 (not_1_out, clk);
  Register #(.width(1)) register_2 (.D(counter_2_q), .Q(Q), .clk(not_2_out), .clr(counter_2_q));  // open: en
  not not_2 (not_2_out, in_1);
  sec_state sec_state_1 (
    .a(register_3_q[1]), .b(register_3_q[0]), .c(in_2[1]), .d(in_2[0]), .e(sec_state_1_f[1]),
    .f(sec_state_1_f[0]));
  Comparator #(.width(1), .mode("unsigned")) comparator_1 (
    .a(register_1_q), .b(counter_1_q), .gt(comparator_1_gt), .lt(comparator_1_lt));  // open: eq
  Register #(.width(2)) register_3 (.D(sec_state_1_f), .Q(register_3_q), .clk(clk), .clr(in_1));  // open: en
  or or_1 (or_1_out, comparator_1_gt, comparator_1_lt);
  Comparator #(.width(1), .mode("unsigned")) comparator_2 (
    .a(Q), .b(counter_2_q), .gt(comparator_2_gt), .lt(comparator_2_lt));  // open: eq
  and and_1 (clr2, or_1_out, in_1);
  or or_2 (clr1, comparator_2_gt, comparator_2_lt);
  \output  output_1 (.a(register_3_q[1]), .b(register_3_q[0]), .c(in_2[1]), .d(in_2[0]), .e(out_3));
  or or_3 (re, clr2, clr1);

  // Other names for the same wires on the sheet: CLR = in_1; input[1:0] = in_2
endmodule
