// Logisim project full_add.circ as structural Verilog: 3 circuits, main circuit main
module main (
  input  x,
  input  y,
  input  z,
  output a,
  output b
);

  wire and_1_out, and_2_out, and_3_out, and_4_out, not_1_out, or_1_out, or_2_out;

  and and_1 (and_1_out, x, y);
  or or_1 (or_1_out, y, x);
  and and_2 (and_2_out, or_1_out, z);
  or or_2 (or_2_out, or_1_out, z);
  and and_3 (and_3_out, z, and_1_out);
  or or_3 (a, and_1_out, and_2_out);
  not not_1 (not_1_out, a);
  and and_4 (and_4_out, not_1_out, or_2_out);
  or or_4 (b, and_4_out, and_3_out);
endmodule

module unknown (
  input  x,
  input  y,
  input  z,
  output a,
  output b
);

  wire main_1_a, main_1_b;

  main main_1 (.a(main_1_a), .b(main_1_b));  // open: x, y, z
  main main_2 ();  // open: x, y, z, a, b
endmodule

module main1 (
  input  x,
  input  y,
  input  z,
  output a,
  output b
);

  wire and_1_out, and_2_out, and_3_out, and_4_out, and_5_out, and_6_out, nor_1_out, or_1_out, or_2_out,
       or_4_out;

  or or_1 (or_1_out, y, x);
  or or_2 (or_2_out, y, x);
  and and_1 (and_1_out, x, y);
  and and_2 (and_2_out, or_1_out, z);
  and and_3 (and_3_out, x, y);
  and and_4 (and_4_out, or_2_out, z);
  or or_3 (a, and_1_out, and_2_out);
  nor nor_1 (nor_1_out, and_3_out, and_4_out);
  or or_4 (or_4_out, y, x, z);
  and and_5 (and_5_out, nor_1_out, or_4_out);
  and and_6 (and_6_out, x, y, z);
  or or_5 (b, and_5_out, and_6_out);
endmodule
