// Logisim project quick.circ as structural Verilog: 8 circuits, main circuit main
module main (
  input  [31:0] in_1,
  output [31:0] out_2
);

  wire CLK, controlled_buffer_1_out, EN, \end , not_1_out;
  wire [31:0] controlled_buffer_2_out, divide2, in1, in2, in3, in4, in5, in6, in7, in8, init_1_out_4,
       init_2_out_4, init_3_out_4, init_4_out_4, init_5_out_4, init_6_out_4, N_1_out, N_q, out1, out2, out3,
       out4, out5, out6, out7, out8;

  init init_1 (.in_1(CLK), .in_2(32'h1), .in_3(in1), .out_4(init_1_out_4));
  Register #(.width(32)) register_1 (.D(init_1_out_4), .Q(out1), .clk(CLK));  // open: en, clr
  init init_2 (.in_1(CLK), .in_2(32'h1), .in_3(in5), .out_4(init_2_out_4));
  Register #(.width(32)) register_2 (.D(init_2_out_4), .en(EN), .Q(out5), .clk(CLK));  // open: clr
  assign controlled_buffer_1_out = \end  ? CLK : 1'bz;  // Controlled_Buffer controlled_buffer_1
  Clock clock_1 (.out(CLK));
  Register #(.width(32)) register_3 (.D(in6), .en(EN), .Q(out6), .clk(controlled_buffer_1_out));  // open: clr
  init init_3 (.in_1(CLK), .in_2(32'h1), .in_3(in2), .out_4(init_3_out_4));
  Register #(.width(32)) register_4 (.D(init_3_out_4), .Q(out2), .clk(CLK));  // open: en, clr
  Register #(.width(32)) register_5 (.D(in7), .en(EN), .Q(out7), .clk(CLK));  // open: clr
  Shifter #(.width(32), .shift("lr")) shifter_1 (.in(N_q), .\dist (5'b00001), .out(divide2));
  init init_4 (.in_1(CLK), .in_2(in_1), .in_3(divide2), .out_4(init_4_out_4));
  Comparator #(.width(32), .mode("unsigned")) comparator_1 (.a({32{1'b0}}), .b(N_q), .lt(\end ));  // open: gt, eq
  Register #(.width(32)) N (.D(init_4_out_4), .Q(N_q), .clk(CLK));  // open: en, clr
  Register #(.width(32)) register_6 (.D(init_5_out_4), .Q(out3), .clk(CLK));  // open: en, clr
  init init_5 (.in_1(CLK), .in_2(32'h1), .in_3(in3), .out_4(init_5_out_4));
  init init_6 (.in_1(CLK), .in_2(32'h1), .in_3(in8), .out_4(init_6_out_4));
  Register #(.width(32)) register_7 (.D(init_6_out_4), .en(EN), .Q(out8), .clk(CLK));  // open: clr
  assign controlled_buffer_2_out = \end  ? N_q : 32'bz;  // Controlled_Buffer controlled_buffer_2
  assign N_1_out = controlled_buffer_2_out & 32'h1;  // AND_Gate N_1, 32 bits wide
  Bit_Extender #(.in_width(32), .out_width(1)) bit_extender_1 (.in(N_1_out), .out(EN));
  Register #(.width(32)) register_8 (.D(in4), .Q(out4), .clk(CLK));  // open: en, clr
  not not_1 (not_1_out, \end );
  square SQ (.in_1(out1), .in_2(out2), .in_3(out3), .in_4(out4), .out_5(in1), .out_6(in2), .out_7(in3), .out_8(in4));
  muliti MULT (
    .in_1(out1), .in_2(out2), .in_3(out3), .in_4(out4), .in_5(out5), .in_6(out6), .in_7(out7), .in_8(out8),
    .out_9(in5), .out_10(in6), .out_11(in7), .out_12(in8));
  Multiplexer #(.width(32)) multiplexer_1 (.in0({32{1'b0}}), .in1(out6), .out(out_2), .sel(not_1_out), .en(1'b1));

  // Other names for the same wires on the sheet: input[31:0] = in_1
endmodule

module square (
  input  [31:0] in_1,
  input  [31:0] in_2,
  input  [31:0] in_3,
  input  [31:0] in_4,
  output [31:0] out_5,
  output [31:0] out_6,
  output [31:0] out_7,
  output [31:0] out_8
);

  wire [31:0] multiplier_1_out, multiplier_2_out, multiplier_3_out, multiplier_4_out, multiplier_5_out,
       multiplier_6_out, multiplier_7_out, multiplier_8_out;

  Multiplier #(.width(32)) multiplier_1 (.a(in_1), .b(in_1), .out(multiplier_1_out));  // open: cin, cout
  Multiplier #(.width(32)) multiplier_2 (.a(in_2), .b(in_3), .out(multiplier_2_out));  // open: cin, cout
  Multiplier #(.width(32)) multiplier_3 (.a(in_1), .b(in_2), .out(multiplier_3_out));  // open: cin, cout
  Multiplier #(.width(32)) multiplier_4 (.a(in_2), .b(in_4), .out(multiplier_4_out));  // open: cin, cout
  Multiplier #(.width(32)) multiplier_5 (.a(in_3), .b(in_1), .out(multiplier_5_out));  // open: cin, cout
  Multiplier #(.width(32)) multiplier_6 (.a(in_4), .b(in_3), .out(multiplier_6_out));  // open: cin, cout
  Multiplier #(.width(32)) multiplier_7 (.a(in_2), .b(in_3), .out(multiplier_7_out));  // open: cin, cout
  Multiplier #(.width(32)) multiplier_8 (.a(in_4), .b(in_4), .out(multiplier_8_out));  // open: cin, cout
  Adder #(.width(32)) adder_1 (.a(multiplier_1_out), .b(multiplier_2_out), .out(out_5));  // open: cin, cout
  Adder #(.width(32)) adder_2 (.a(multiplier_3_out), .b(multiplier_4_out), .out(out_6));  // open: cin, cout
  Adder #(.width(32)) adder_3 (.a(multiplier_5_out), .b(multiplier_6_out), .out(out_7));  // open: cin, cout
  Adder #(.width(32)) adder_4 (.a(multiplier_7_out), .b(multiplier_8_out), .out(out_8));  // open: cin, cout
endmodule

module muliti (
  input  [31:0] in_1,
  input  [31:0] in_2,
  input  [31:0] in_3,
  input  [31:0] in_4,
  input  [31:0] in_5,
  input  [31:0] in_6,
  input  [31:0] in_7,
  input  [31:0] in_8,
  output [31:0] out_9,
  output [31:0] out_10,
  output [31:0] out_11,
  output [31:0] out_12
);

  wire [31:0] multiplier_1_out, multiplier_2_out, multiplier_3_out, multiplier_4_out, multiplier_5_out,
       multiplier_6_out, multiplier_7_out, multiplier_8_out;

  Multiplier #(.width(32)) multiplier_1 (.a(in_1), .b(in_5), .out(multiplier_1_out));  // open: cin, cout
  Multiplier #(.width(32)) multiplier_2 (.a(in_2), .b(in_7), .out(multiplier_2_out));  // open: cin, cout
  Multiplier #(.width(32)) multiplier_3 (.a(in_1), .b(in_6), .out(multiplier_3_out));  // open: cin, cout
  Multiplier #(.width(32)) multiplier_4 (.a(in_2), .b(in_8), .out(multiplier_4_out));  // open: cin, cout
  Multiplier #(.width(32)) multiplier_5 (.a(in_3), .b(in_5), .out(multiplier_5_out));  // open: cin, cout
  Multiplier #(.width(32)) multiplier_6 (.a(in_4), .b(in_7), .out(multiplier_6_out));  // open: cin, cout
  Multiplier #(.width(32)) multiplier_7 (.a(in_3), .b(in_6), .out(multiplier_7_out));  // open: cin, cout
  Multiplier #(.width(32)) multiplier_8 (.a(in_4), .b(in_8), .out(multiplier_8_out));  // open: cin, cout
  Adder #(.width(32)) adder_1 (.a(multiplier_1_out), .b(multiplier_2_out), .out(out_9));  // open: cin, cout
  Adder #(.width(32)) adder_2 (.a(multiplier_3_out), .b(multiplier_4_out), .out(out_10));  // open: cin, cout
  Adder #(.width(32)) adder_3 (.a(multiplier_5_out), .b(multiplier_6_out), .out(out_11));  // open: cin, cout
  Adder #(.width(32)) adder_4 (.a(multiplier_7_out), .b(multiplier_8_out), .out(out_12));  // open: cin, cout
endmodule

module ceshi (
  input  [31:0] in_1,
  input  [31:0] in_2,
  input  [31:0] in_3,
  input  [31:0] in_4,
  input  [31:0] in_5,
  input  [31:0] in_6,
  input  [31:0] in_7,
  input  [31:0] in_8,
  output [31:0] out_9,
  output [31:0] out_10,
  output [31:0] out_11,
  output [31:0] out_12
);

  muliti muliti_1 (
    .in_1(in_1), .in_2(in_2), .in_3(in_3), .in_4(in_4), .in_5(in_5), .in_6(in_6), .in_7(in_7), .in_8(in_8),
    .out_9(out_9), .out_10(out_10), .out_11(out_11), .out_12(out_12));
endmodule

module ceshi1 (
  input  [31:0] in_1,
  input  [31:0] in_2,
  input  [31:0] in_3,
  input  [31:0] in_4,
  output [31:0] out_5,
  output [31:0] out_6,
  output [31:0] out_7,
  output [31:0] out_8
);

  square square_1 (
    .in_1(in_1), .in_2(in_2), .in_3(in_3), .in_4(in_4), .out_5(out_5), .out_6(out_6), .out_7(out_7),
    .out_8(out_8));
endmodule

module init (
  input  in_1,
  input  [31:0] in_2,
  input  [31:0] in_3,
  output [31:0] out_4
);

  wire not_1_out, not_2_out, register_1_q;

  Register #(.width(1)) register_1 (.D(1'b1), .Q(register_1_q), .clk(not_1_out));  // open: en, clr
  not not_1 (not_1_out, in_1);
  Multiplexer #(.width(32)) multiplexer_1 (.in0(in_2), .in1(in_3), .out(out_4), .sel(register_1_q), .en(not_2_out));
  not not_2 (not_2_out, in_1);

  // Other names for the same wires on the sheet: CLK = in_1; input1[31:0] = in_2; input2[31:0] = in_3
endmodule

module cal (
  input  judge
);

  wire clock_1_out;
  wire [31:0] register_1_q, shifter_1_out, undriven;

  Divider #(.width(32)) divider_1 (.a(undriven), .b(32'h2));  // open: out, upper, rem
  Shifter #(.width(32), .shift("lr")) shifter_1 (.in(register_1_q), .\dist (5'b00001), .out(shifter_1_out));
  Register #(.width(32)) register_1 (.D(shifter_1_out), .Q(register_1_q), .clk(clock_1_out));  // open: en, clr
  Clock clock_1 (.out(clock_1_out));
  // Probe on register_1_q
endmodule

module calc (
  input  [31:0] in_1,
  input  [31:0] in_2,
  input  in_3
);

  wire bit_extender_1_out, controlled_buffer_2_out, not_1_out;
  wire [31:0] and_1_out, controlled_buffer_1_out, controlled_buffer_3_out;

  assign controlled_buffer_1_out = in_3 ? in_1 : 32'bz;  // Controlled_Buffer controlled_buffer_1
  assign and_1_out = 32'h1 & controlled_buffer_1_out;  // AND_Gate and_1, 32 bits wide
  assign controlled_buffer_2_out = bit_extender_1_out ? 1'b1 : 1'bz;  // Controlled_Buffer controlled_buffer_2
  Bit_Extender #(.in_width(32), .out_width(1)) bit_extender_1 (.in(and_1_out), .out(bit_extender_1_out));
  not not_1 (not_1_out, bit_extender_1_out);
  assign controlled_buffer_3_out = not_1_out ? in_2 : 32'bz;  // Controlled_Buffer controlled_buffer_3
  square square_1 ();  // open: in_1, in_2, in_3, in_4, out_5, out_6, out_7, out_8
  muliti muliti_1 ();  // open: in_1, in_2, in_3, in_4, in_5, in_6, in_7, in_8, out_9, out_10, out_11, out_12
endmodule
