// Logisim project swap.circ as structural Verilog: 4 circuits, main circuit 1bit_swap
module _4bit_swap (
  input  [3:0] in_1,
  input  [3:0] in_2,
  input  in_3,
  output [3:0] out_4,
  output [3:0] out_5
);

  _1bit_swap u_1bit_swap_1 (.I1(in_1[0]), .I2(in_2[0]), .S(in_3), .O1(out_4[0]), .O2(out_5[0]));
  _1bit_swap u_1bit_swap_2 (.I1(in_1[1]), .I2(in_2[1]), .S(in_3), .O1(out_4[1]), .O2(out_5[1]));
  _1bit_swap u_1bit_swap_3 (.I1(in_1[2]), .I2(in_2[2]), .S(in_3), .O1(out_4[2]), .O2(out_5[2]));
  _1bit_swap u_1bit_swap_4 (.I1(in_1[3]), .I2(in_2[3]), .S(in_3), .O1(out_4[3]), .O2(out_5[3]));

  // Other names for the same wires on the sheet: S = in_3
endmodule

module _1bit_swap (
  input  I1,
  input  I2,
  input  S,
  output O1,
  output O2
);

  wire _1, and_1_out, and_2_out, and_3_out, and_4_out;

  not not_1 (_1, S);
  and and_1 (and_1_out, I1, _1);
  and and_2 (and_2_out, S, I2);
  and and_3 (and_3_out, I1, S);
  and and_4 (and_4_out, _1, I2);
  or or_1 (O1, and_1_out, and_2_out);
  or or_2 (O2, and_3_out, and_4_out);

  // Other names for the same wires on the sheet: _2 = S
endmodule

module _4bit_sort (
  input  [3:0] in_1,
  input  [3:0] in_2,
  input  [3:0] in_3,
  input  [3:0] in_4,
  output [3:0] out_5,
  output [3:0] out_6,
  output [3:0] out_7,
  output [3:0] out_8
);

  wire [3:0] n2input_compare_1_out_3, n2input_compare_1_out_4, n2input_compare_2_out_3,
       n2input_compare_2_out_4, n2input_compare_3_out_3, n2input_compare_3_out_4, n2input_compare_4_out_4,
       n2input_compare_5_out_4;

  _2input_compare u_2input_compare_1 (
    .in_1(in_1), .in_2(in_2), .out_3(n2input_compare_1_out_3), .out_4(n2input_compare_1_out_4));
  _2input_compare u_2input_compare_2 (
    .in_1(n2input_compare_1_out_3), .in_2(in_3), .out_3(n2input_compare_2_out_3),
    .out_4(n2input_compare_2_out_4));
  _2input_compare u_2input_compare_3 (
    .in_1(n2input_compare_1_out_4), .in_2(n2input_compare_2_out_4), .out_3(n2input_compare_3_out_3),
    .out_4(n2input_compare_3_out_4));
  _2input_compare u_2input_compare_4 (
    .in_1(n2input_compare_2_out_3), .in_2(in_4), .out_3(out_5), .out_4(n2input_compare_4_out_4));
  _2input_compare u_2input_compare_5 (
    .in_1(n2input_compare_3_out_3), .in_2(n2input_compare_4_out_4), .out_3(out_6),
    .out_4(n2input_compare_5_out_4));
  _2input_compare u_2input_compare_6 (
    .in_1(n2input_compare_5_out_4), .in_2(n2input_compare_3_out_4), .out_3(out_7), .out_4(out_8));
endmodule

module _2input_compare (
  input  [3:0] in_1,
  input  [3:0] in_2,
  output [3:0] out_3,
  output [3:0] out_4
);

  wire comparator_1_gt;

  Comparator #(.width(4), .mode("unsigned")) comparator_1 (.a(in_1), .b(in_2), .gt(comparator_1_gt));  // open: eq, lt
  _4bit_swap u_4bit_swap_1 (.in_1(in_1), .in_2(in_2), .in_3(comparator_1_gt), .out_4(out_3), .out_5(out_4));
endmodule
