// Logisim project swap1(control).circ as structural Verilog: 1 circuit, main circuit main
module main (
  input  in_1,
  input  in_2,
  output out_3,
  output out_4
);

  wire not_1_out;

  assign out_3 = not_1_out ? in_1 : 1'bz;  // Controlled_Buffer controlled_buffer_1
  not not_1 (not_1_out, in_2);
  assign out_4 = in_2 ? in_1 : 1'bz;  // Controlled_Buffer controlled_buffer_2
endmodule
