// Logisim project transfer.circ as structural Verilog
module main (
  input  [15:0] in_1,
  input  [3:0] in_2,
  output [15:0] out_3,
  output [15:0] out_4
);

  wire _2;
  wire [15:0] demultiplexer_1_out0;

  Demultiplexer #(.width(16)) demultiplexer_1 (
    .out0(demultiplexer_1_out0), .out1({_2, out_4[15:1]}), .in(in_1), .sel(1'b0));  // open: en
  assign out_3 = {out_4[15:1], 1'b0} | demultiplexer_1_out0;  // OR_Gate or_1, 16 bits wide

  assign out_4[0] = 1'b0;
endmodule
